// Logisim project principal.circ as structural Verilog: 3 circuits, main circuit main
module main (
  input  Confirmar,
  input  in_2,
  input  [3:0] in_3,
  output [7:0] out_4,
  output [7:0] out_5,
  output out_6,
  output out_7,
  output out_8,
  output out_9,
  output out_10,
  output out_11,
  output out_12,
  output out_13
);

  wire comparador_1_p2, \modulo_da_diferença_1_p3 ;
  wire [3:0] random_1_out;
  wire [7:0] main_1_p1, main_1_p2, sinal_estendido_1_out_2;

  Random #(.width(4)) random_1 (.clk(in_2), .out(random_1_out));  // open: next, clr
  assign out_4 = main_1_p1 & sinal_estendido_1_out_2;  // AND_Gate and_1, 8 bits wide
  Sinal_Estendido sinal_estendido_1 (.in_1(Confirmar), .out_2(sinal_estendido_1_out_2));
  // modulo_da_diferença modulo_da_diferença_1: pin names not known; wires that end beside it: random_1_out, in_3, \modulo_da_diferença_1_p3 , random_1_out, in_3
  assign out_5 = main_1_p2 & sinal_estendido_1_out_2;  // AND_Gate and_2, 8 bits wide
  // Cores_main main_1: pin names not known; wires that end beside it: main_1_p1, main_1_p2
  // comparador comparador_1: pin names not known; wires that end beside it: \modulo_da_diferença_1_p3 , comparador_1_p2
  // decoder_com_4_bits decoder_com_4_bits_1: pin names not known; wires that end beside it: in_3, out_7, out_8, out_9, out_10, out_11, out_12, out_13
  and and_3 (out_6, Confirmar, comparador_1_p2);
endmodule

module Sinal_Estendido (
  input  in_1,
  output [7:0] out_2
);


  assign out_2 = {8{in_1}};
endmodule

module jogo (
  input  in_1,
  input  [3:0] in_2
);

  wire button_1_out, main_1_out_6, main_1_out_7, main_1_out_8, main_1_out_9, main_1_out_10, main_1_out_11,
       main_1_out_12, main_1_out_13;
  wire [7:0] rgbled_1_p1, rgbled_1_p2;

  Button button_1 (.out(button_1_out));
  LED led_1 (.in(main_1_out_6));
  // RGBLed #(.multibit("true")) rgbled_1: pin names not known; wires that end beside it: rgbled_1_p1, rgbled_1_p2
  main main_1 (
    .Confirmar(in_1), .in_2(button_1_out), .in_3(in_2), .out_7(main_1_out_7), .out_8(main_1_out_8),
    .out_9(main_1_out_9), .out_10(main_1_out_10), .out_11(main_1_out_11), .out_12(main_1_out_12),
    .out_13(main_1_out_13), .out_4(rgbled_1_p2), .out_5(rgbled_1_p1), .out_6(main_1_out_6));
  _7_Segment_Display u_7_segment_display_1 (
    .g(main_1_out_13), .f(main_1_out_12), .a(main_1_out_7), .b(main_1_out_8), .e(main_1_out_11),
    .d(main_1_out_10), .c(main_1_out_9));  // open: dp
endmodule
